// Digital circuit Ecuación_1.dig as structural Verilog
module \Ecuación_1  (
  input  A,
  input  B,
  input  C,
  output Y
);

  wire and_1_out, not_1_out, not_2_out, not_3_out, or_1_out;

  not not_1 (not_1_out, C);
  or or_1 (or_1_out, B, not_1_out);
  and and_1 (and_1_out, A, or_1_out);
  not not_2 (not_2_out, and_1_out);
  not not_3 (not_3_out, B);
  xor xor_1 (Y, not_2_out, not_3_out);

  // Notes on the sheet:
  //   Y = (not (A and (B or not C) ) ) xor (not B))
endmodule

/* Test case Y:
C B A Y 

 0 0 0 0
 0 0 1 1
 0 1 0 1
 0 1 1 0
 1 0 0 0
 1 0 1 0
 1 1 0 1
 1 1 1 0
*/
