// Digital circuit Ecuación_10.dig as structural Verilog
module \Ecuación_10  (
  input  C,
  input  B,
  input  A,
  output Y
);

  wire xnor_1_out;

  xnor xnor_1 (xnor_1_out, B, C);
  and and_1 (Y, A, xnor_1_out);

  // Notes on the sheet:
  //   Y = A . not(B xor C)
endmodule

/* Test case Ecuacion 10:
C B A Y 

 0 0 0 0
 0 0 1 1
 0 1 0 0
 0 1 1 0
 1 0 0 0
 1 0 1 0
 1 1 0 0
 1 1 1 1
*/
