// Digital circuit Ecuación_11.dig as structural Verilog
module \Ecuación_11  (
  input  D,
  input  C,
  input  B,
  input  A,
  output Y
);

  wire and_1_out, nand_1_out, not_3_out, not_4_out, or_1_out;

  // Not not_1 has open pins: in=D, out=open
  // Not not_2 has open pins: in=C, out=open
  not not_3 (not_3_out, B);
  not not_4 (not_4_out, A);
  nand nand_1 (nand_1_out, not_3_out, C);
  or or_1 (or_1_out, nand_1_out, D);
  and and_1 (and_1_out, not_4_out, C);
  xor xor_1 (Y, or_1_out, and_1_out);

  // Notes on the sheet:
  //   Y = (D or not(C and not B) ) xor (not A and C)
endmodule

/* Test case Ecuacion 11:
D C B A Y 

 0 0 0 0 1
 0 0 0 1 1
 0 0 1 0 1
 0 0 1 1 1
 0 1 0 0 1
 0 1 0 1 0
 0 1 1 0 0
 0 1 1 1 1
 1 0 0 0 1
 1 0 0 1 1
 1 0 1 0 1
 1 0 1 1 1
 1 1 0 0 0
 1 1 0 1 1
 1 1 1 0 0
 1 1 1 1 1
*/
