// Digital circuit Ecuación_12.dig as structural Verilog
module \Ecuación_12  (
  input  D,
  input  C,
  input  B,
  input  A,
  output Y
);

  wire and_1_out, and_2_out, and_3_out, and_4_out, nand_1_out, nand_2_out, nor_1_out, not_2_out, not_3_out,
       or_1_out;

  // Not not_1 has open pins: in=D, out=open
  not not_2 (not_2_out, C);
  not not_3 (not_3_out, B);
  // Not not_4 has open pins: in=A, out=open
  nand nand_1 (nand_1_out, A, C);
  and and_1 (and_1_out, A, C);
  nor nor_1 (nor_1_out, and_1_out, B);
  and and_2 (and_2_out, D, nand_1_out);
  and and_3 (and_3_out, A, not_3_out);
  and and_4 (and_4_out, and_2_out, nor_1_out);
  nand nand_2 (nand_2_out, A, B, not_2_out);
  or or_1 (or_1_out, and_3_out, and_4_out);
  and and_5 (Y, nand_2_out, or_1_out);

  // Notes on the sheet:
  //   Y = not(A . B . not C) . ((A . not B) + D . not(A . C) . not(C . A + B))
endmodule

/* Test case Ecuacion 12:
D C B A Y 

 0 0 0 0 0
 0 0 0 1 1
 0 0 1 0 0
 0 0 1 1 0
 0 1 0 0 0
 0 1 0 1 1
 0 1 1 0 0
 0 1 1 1 0
 1 0 0 0 1
 1 0 0 1 1
 1 0 1 0 0
 1 0 1 1 0
 1 1 0 0 1
 1 1 0 1 1
 1 1 1 0 0
 1 1 1 1 0
*/
