// Digital circuit Ecuación_13.dig as structural Verilog
module \Ecuación_13  (
  input  D,
  input  C,
  input  B,
  input  A,
  output Y
);

  wire nand_1_out, nand_2_out, nand_3_out, nor_1_out, not_2_out, not_3_out;

  // Not not_1 has open pins: in=D, out=open
  not not_2 (not_2_out, C);
  not not_3 (not_3_out, B);
  // Not not_4 has open pins: in=A, out=open
  nand nand_1 (nand_1_out, B, not_2_out);
  nand nand_2 (nand_2_out, A, not_3_out);
  nand nand_3 (nand_3_out, A, nand_1_out);
  nor nor_1 (nor_1_out, D, nand_2_out);
  and and_1 (Y, nand_3_out, nor_1_out);

  // Notes on the sheet:
  //   Y = not(A . not(B . not C) ) . not(D + not(A . not B) )
endmodule

/* Test case Ecuacion 13:
D C B A Y 

 0 0 0 0 0
 0 0 0 1 0
 0 0 1 0 0
 0 0 1 1 0
 0 1 0 0 0
 0 1 0 1 0
 0 1 1 0 0
 0 1 1 1 0
 1 0 0 0 0
 1 0 0 1 0
 1 0 1 0 0
 1 0 1 1 0
 1 1 0 0 0
 1 1 0 1 0
 1 1 1 0 0
 1 1 1 1 0
*/
