// Digital circuit Ecuación_14.dig as structural Verilog
module \Ecuación_14  (
  input  D,
  input  C,
  input  B,
  input  A,
  output Y
);

  wire nand_1_out, nand_2_out, nand_3_out, nor_1_out, nor_2_out, nor_3_out, not_4_out;

  // Not not_1 has open pins: in=D, out=open
  // Not not_2 has open pins: in=C, out=open
  // Not not_3 has open pins: in=B, out=open
  not not_4 (not_4_out, A);
  nand nand_1 (nand_1_out, not_4_out, B);
  nor nor_1 (nor_1_out, not_4_out, B);
  nand nand_2 (nand_2_out, nand_1_out, C);
  nor nor_2 (nor_2_out, C, nor_1_out);
  nand nand_3 (nand_3_out, nand_2_out, D);
  nor nor_3 (nor_3_out, D, nor_2_out);
  and and_1 (Y, nand_3_out, nor_3_out);

  // Notes on the sheet:
  //   Y = (not(not(not(not A . B) . C ) - D ) ) . (not(not(not(not A + B) + C) + D) )
endmodule

/* Test case Ecuacion 14:
D C B A Y 

 0 0 0 0 0
 0 0 0 1 1
 0 0 1 0 0
 0 0 1 1 0
 0 1 0 0 1
 0 1 0 1 1
 0 1 1 0 1
 0 1 1 1 1
 1 0 0 0 0
 1 0 0 1 0
 1 0 1 0 0
 1 0 1 1 0
 1 1 0 0 0
 1 1 0 1 0
 1 1 1 0 0
 1 1 1 1 0
*/
