// Digital circuit Ecuación_15.dig as structural Verilog
module \Ecuación_15  (
  input  D,
  input  C,
  input  B,
  input  A,
  output Y
);

  wire nand_1_out, nand_2_out, nor_1_out, not_1_out;

  not not_1 (not_1_out, B);
  nand nand_1 (nand_1_out, A, B);
  nand nand_2 (nand_2_out, nand_1_out, C);
  nor nor_1 (nor_1_out, not_1_out, D);
  xor xor_1 (Y, nand_2_out, nor_1_out);

  // Notes on the sheet:
  //   Y = (not( not(A . B) . C) ) xor (not(not B + D) )
endmodule

/* Test case Ecuacion 15:
D C B A Y 

 0 0 0 0 1
 0 0 0 1 1
 0 0 1 0 0
 0 0 1 1 0
 0 1 0 0 0
 0 1 0 1 0
 0 1 1 0 1
 0 1 1 1 0
 1 0 0 0 1
 1 0 0 1 1
 1 0 1 0 1
 1 0 1 1 1
 1 1 0 0 0
 1 1 0 1 0
 1 1 1 0 0
 1 1 1 1 1
*/
