// Digital circuit Ecuación_16.dig as structural Verilog
module \Ecuación_16  (
  input  D,
  input  C,
  input  B,
  input  A,
  output Y
);

  wire and_1_out, nand_1_out, nor_1_out, not_2_out, not_3_out, not_4_out, or_1_out;

  // Not not_1 has open pins: in=D, out=open
  not not_2 (not_2_out, C);
  not not_3 (not_3_out, B);
  not not_4 (not_4_out, A);
  and and_1 (and_1_out, not_3_out, D);
  nand nand_1 (nand_1_out, not_4_out, C);
  or or_1 (or_1_out, and_1_out, nand_1_out);
  nor nor_1 (nor_1_out, A, B, not_2_out);
  xor xor_1 (Y, or_1_out, nor_1_out);

  // Notes on the sheet:
  //   Y = (D . not B + not( not A . C) ) xor (not( not C + B +A) )
endmodule

/* Test case Ecuacion 16:
D C B A Y 

 0 0 0 0 1
 0 0 0 1 1
 0 0 1 0 1
 0 0 1 1 1
 0 1 0 0 1
 0 1 0 1 1
 0 1 1 0 0
 0 1 1 1 1
 1 0 0 0 1
 1 0 0 1 1
 1 0 1 0 1
 1 0 1 1 1
 1 1 0 0 0
 1 1 0 1 1
 1 1 1 0 0
 1 1 1 1 1
*/
