// Digital circuit Ecuación_17.dig as structural Verilog
module \Ecuación_17  (
  input  C,
  input  B,
  input  A,
  output Y
);

  wire and_1_out, and_2_out, nand_1_out, nor_1_out;

  nand nand_1 (nand_1_out, B, C);
  and and_1 (and_1_out, A, ~C);  // And
  nor nor_1 (nor_1_out, nand_1_out, and_1_out);
  and and_2 (and_2_out, ~A, B);  // And
  nor nor_2 (Y, nor_1_out, and_2_out);
endmodule

/* Test case Ecuacion 17:
C B A Y 

 0 0 0 1
 0 0 1 1
 0 1 0 0
 0 1 1 1
 1 0 0 1
 1 0 1 1
 1 1 0 0
 1 1 1 0
*/
