// Digital circuit Ecuación_18.dig as structural Verilog
module \Ecuación_18  (
  input  D,
  input  C,
  input  B,
  input  A,
  output Y
);

  wire nand_1_out, nand_2_out, nand_3_out, nand_4_out;

  nand nand_1 (nand_1_out, A, B);
  nand nand_2 (nand_2_out, ~B, ~C);  // NAnd
  nand nand_3 (nand_3_out, nand_1_out, C);
  nand nand_4 (nand_4_out, ~D, nand_2_out);  // NAnd
  xor xor_1 (Y, nand_3_out, nand_4_out);

  // Notes on the sheet:
  //   Y = (not(not(A . B) . C ) ) xor (not(not( not B . not C) not D ) )
endmodule

/* Test case Ecuacion 18:
D C B A Y 

 0 0 0 0 0
 0 0 0 1 0
 0 0 1 0 1
 0 0 1 1 1
 0 1 0 0 0
 0 1 0 1 0
 0 1 1 0 0
 0 1 1 1 1
 1 0 0 0 0
 1 0 0 1 0
 1 0 1 0 0
 1 0 1 1 0
 1 1 0 0 1
 1 1 0 1 1
 1 1 1 0 1
 1 1 1 1 0
*/
