// Digital circuit Ecuación_19.dig as structural Verilog
module \Ecuación_19  (
  input  D,
  input  C,
  input  B,
  input  A,
  output Y
);

  wire nand_1_out, nand_2_out;

  nand nand_1 (nand_1_out, ~A, B);  // NAnd
  nand nand_2 (nand_2_out, nand_1_out, C);
  nand nand_3 (Y, nand_2_out, D);

  // Notes on the sheet:
  //   Y = not( not( not( not A . B) . C) . D)
endmodule

/* Test case Ecuacion 19:
D C B A Y 

 0 0 0 0 1
 0 0 0 1 1
 0 0 1 0 1
 0 0 1 1 1
 0 1 0 0 1
 0 1 0 1 1
 0 1 1 0 1
 0 1 1 1 1
 1 0 0 0 0
 1 0 0 1 0
 1 0 1 0 0
 1 0 1 1 0
 1 1 0 0 1
 1 1 0 1 1
 1 1 1 0 0
 1 1 1 1 1
*/
