// Digital circuit Ecuación_2.dig as structural Verilog
module \Ecuación_2  (
  input  A,
  input  B,
  input  C,
  output Y
);

  wire and_1_out, not_1_out, not_2_out, or_1_out;

  not not_1 (not_1_out, C);
  or or_1 (or_1_out, B, not_1_out);
  not not_2 (not_2_out, or_1_out);
  and and_1 (and_1_out, A, not_2_out);
  not not_3 (Y, and_1_out);

  // Notes on the sheet:
  //   Y = not(A and not(B or not C) )
endmodule

/* Test case Ecuacion 2:
C B A Y 

 0 0 0 1
 0 0 1 1
 0 1 0 1
 0 1 1 1
 1 0 0 1
 1 0 1 0
 1 1 0 1
 1 1 1 1
*/
