// Digital circuit Ecuación_20.dig as structural Verilog
module \Ecuación_20  (
  input  D,
  input  C,
  input  B,
  input  A,
  output Y
);

  wire nor_1_out, nor_2_out;

  nor nor_1 (nor_1_out, ~A, B);  // NOr
  nor nor_2 (nor_2_out, nor_1_out, C);
  nor nor_3 (Y, nor_2_out, D);

  // Notes on the sheet:
  //   Y = not( not( not( not A + B) + C) + D)
endmodule

/* Test case Ecuacion 20:
D C B A Y 

 0 0 0 0 0
 0 0 0 1 1
 0 0 1 0 0
 0 0 1 1 0
 0 1 0 0 1
 0 1 0 1 1
 0 1 1 0 1
 0 1 1 1 1
 1 0 0 0 0
 1 0 0 1 0
 1 0 1 0 0
 1 0 1 1 0
 1 1 0 0 0
 1 1 0 1 0
 1 1 1 0 0
 1 1 1 1 0
*/
