// Digital circuit Ecuación_21.dig as structural Verilog
module \Ecuación_21  (
  input  C,
  input  B,
  input  A,
  output Y
);

  wire xor_1_out;

  xor xor_1 (xor_1_out, A, B);
  xor xor_2 (Y, xor_1_out, C);

  // Notes on the sheet:
  //   Y = (A xor B) xor C
endmodule

/* Test case Ecuacion 21:
C B A Y 

 0 0 0 0
 0 0 1 1
 0 1 0 1
 0 1 1 0
 1 0 0 1
 1 0 1 0
 1 1 0 0
 1 1 1 1
*/
