// Digital circuit Ecuación_22.dig as structural Verilog
module \Ecuación_22  (
  input  D,
  input  C,
  input  B,
  input  A,
  output Y
);

  wire and_1_out, nand_1_out, or_1_out;

  nand nand_1 (nand_1_out, ~B, C);  // NAnd
  and and_1 (and_1_out, ~A, C);  // And
  or or_1 (or_1_out, nand_1_out, D);
  xor xor_1 (Y, and_1_out, or_1_out);

  // Notes on the sheet:
  //   Y = (C . not A) xor ( not(C . not B) + D)
endmodule

/* Test case Ecuacion 22:
D C B A Y 

 0 0 0 0 1
 0 0 0 1 1
 0 0 1 0 1
 0 0 1 1 1
 0 1 0 0 1
 0 1 0 1 0
 0 1 1 0 0
 0 1 1 1 1
 1 0 0 0 1
 1 0 0 1 1
 1 0 1 0 1
 1 0 1 1 1
 1 1 0 0 0
 1 1 0 1 1
 1 1 1 0 0
 1 1 1 1 1
*/
