// Digital circuit Ecuación_23.dig as structural Verilog
module \Ecuación_23  (
  input  D,
  input  C,
  input  B,
  input  A,
  output Y
);

  wire and_1_out, and_2_out, nand_1_out, nor_1_out;

  nand nand_1 (nand_1_out, A, C);
  and and_1 (and_1_out, A, ~B);  // And
  and and_2 (and_2_out, nand_1_out, B);
  nor nor_1 (nor_1_out, and_1_out, D);
  xor xor_1 (Y, and_2_out, nor_1_out);

  // Notes on the sheet:
  //   Y = (B . not(C . A) ) xor (A . not B + D)
endmodule

/* Test case Ecuacion 23:
D C B A Y 

 0 0 0 0 1
 0 0 0 1 0
 0 0 1 0 0
 0 0 1 1 0
 0 1 0 0 1
 0 1 0 1 0
 0 1 1 0 0
 0 1 1 1 1
 1 0 0 0 0
 1 0 0 1 0
 1 0 1 0 1
 1 0 1 1 1
 1 1 0 0 0
 1 1 0 1 0
 1 1 1 0 1
 1 1 1 1 0
*/
