// Digital circuit Ecuación_24.dig as structural Verilog
module \Ecuación_24  (
  input  C,
  input  B,
  input  A,
  output Y
);

  wire nand_1_out, nor_1_out, or_1_out;

  nand nand_1 (nand_1_out, ~A, B);  // NAnd
  or or_1 (or_1_out, nand_1_out, C);
  nor nor_1 (nor_1_out, ~A, B);  // NOr
  and and_1 (Y, or_1_out, nor_1_out);

  // Notes on the sheet:
  //   Y = (not( not A . B) + C) . (not(B + not A) )
endmodule

/* Test case Ecuacion 24:
C B A Y 

 0 0 0 0
 0 0 1 1
 0 1 0 0
 0 1 1 0
 1 0 0 0
 1 0 1 1
 1 1 0 0
 1 1 1 0
*/
