// Digital circuit Ecuación_25.dig as structural Verilog
module \Ecuación_25  (
  input  D,
  input  C,
  input  B,
  input  A,
  output Y
);

  wire and_1_out, nand_1_out, nand_2_out, nand_3_out, or_1_out;

  nand nand_1 (nand_1_out, C, D);
  nand nand_2 (nand_2_out, B, D);
  nand nand_3 (nand_3_out, B, nand_1_out);
  and and_1 (and_1_out, nand_2_out, A);
  or or_1 (or_1_out, A, nand_3_out);
  xor xor_1 (Y, and_1_out, or_1_out);

  // Notes on the sheet:
  //   Y = (not(D . B) . A) xor (A + not( not(C . D) . B) )
endmodule

/* Test case Ecuacion 25:
D C B A Y 

 0 0 0 0 1
 0 0 0 1 0
 0 0 1 0 0
 0 0 1 1 0
 0 1 0 0 1
 0 1 0 1 0
 0 1 1 0 0
 0 1 1 1 0
 1 0 0 0 1
 1 0 0 1 0
 1 0 1 0 0
 1 0 1 1 1
 1 1 0 0 1
 1 1 0 1 0
 1 1 1 0 1
 1 1 1 1 1
*/
