// Digital circuit Ecuación_26.dig as structural Verilog
module \Ecuación_26  (
  input  C,
  input  B,
  input  A,
  output Y
);

  wire and_1_out, nand_1_out, nor_1_out;

  and and_1 (and_1_out, ~A, B);  // And
  nor nor_1 (nor_1_out, and_1_out, C);
  nand nand_1 (nand_1_out, A, ~B, C);  // NAnd
  and and_2 (Y, nor_1_out, nand_1_out);

  // Notes on the sheet:
  //   Y = not( (not A . B) + C) . not(A . not B . C)
endmodule

/* Test case Ecuacion 26:
C B A Y 

 0 0 0 1
 0 0 1 1
 0 1 0 0
 0 1 1 1
 1 0 0 0
 1 0 1 0
 1 1 0 0
 1 1 1 0
*/
