// Digital circuit Ecuación_3.dig as structural Verilog
module \Ecuación_3  (
  input  A,
  input  B,
  input  C,
  output Y
);

  wire and_1_out, and_2_out, not_1_out, not_2_out;

  not not_1 (not_1_out, C);
  and and_1 (and_1_out, B, not_1_out);
  not not_2 (not_2_out, and_1_out);
  and and_2 (and_2_out, A, not_2_out);
  not not_3 (Y, and_2_out);

  // Notes on the sheet:
  //   Y = not(A and not (B and not C) )
endmodule

/* Test case Ecuacion 3:
C B A Y 

 0 0 0 1
 0 0 1 0
 0 1 0 1
 0 1 1 1
 1 0 0 1
 1 0 1 0
 1 1 0 1
 1 1 1 0
*/
