// Digital circuit Ecuación_4.dig as structural Verilog
module \Ecuación_4  (
  input  A,
  input  B,
  input  C,
  output Y
);

  wire and_1_out, nand_1_out, nand_2_out, nor_1_out;

  nand nand_1 (nand_1_out, A, C);
  nor nor_1 (nor_1_out, B, C);
  and and_1 (and_1_out, B, nand_1_out);
  nand nand_2 (nand_2_out, A, nor_1_out);
  xor xor_1 (Y, and_1_out, nand_2_out);

  // Notes on the sheet:
  //   Y = (B and not(C and A)) xor not(A and not( B or c))
endmodule

/* Test case Ecuacion 4:
C B A Y 

 0 0 0 1
 0 0 1 0
 0 1 0 0
 0 1 1 0
 1 0 0 1
 1 0 1 1
 1 1 0 0
 1 1 1 1
*/
