// Digital circuit Ecuación_5.dig as structural Verilog
module \Ecuación_5  (
  input  A,
  input  B,
  input  C,
  input  D,
  output Y
);

  wire and_1_out, and_2_out, nand_1_out, nor_1_out, nor_2_out;

  nand nand_1 (nand_1_out, A, C);
  nor nor_1 (nor_1_out, B, C);
  and and_1 (and_1_out, B, nand_1_out);
  and and_2 (and_2_out, A, nor_1_out);
  nor nor_2 (nor_2_out, and_2_out, D);
  xor xor_1 (Y, and_1_out, nor_2_out);

  // Notes on the sheet:
  //   Y = (B and not(C and A)) xor not(A and not( B or c) or D)
endmodule

/* Test case Ecuacion 5:
D C B A Y 

 0 0 0 0 1
 0 0 0 1 0
 0 0 1 0 0
 0 0 1 1 0
 0 1 0 0 1
 0 1 0 1 1
 0 1 1 0 0
 0 1 1 1 1
 1 0 0 0 0
 1 0 0 1 0
 1 0 1 0 1
 1 0 1 1 1
 1 1 0 0 0
 1 1 0 1 0
 1 1 1 0 1
 1 1 1 1 0
*/
