// Digital circuit Ecuación_6.dig as structural Verilog
module \Ecuación_6  (
  input  C,
  input  B,
  input  A,
  output Y
);

  wire and_1_out, nor_1_out;

  and and_1 (and_1_out, A, B);
  nor nor_1 (nor_1_out, and_1_out, C);
  xor xor_1 (Y, A, nor_1_out);

  // Notes on the sheet:
  //   Y = ((A and B) or C) xor (A)
endmodule

/* Test case Ecuacion 6:
C B A Y 

 0 0 0 1
 0 0 1 0
 0 1 0 1
 0 1 1 1
 1 0 0 0
 1 0 1 1
 1 1 0 0
 1 1 1 1
*/
