// Digital circuit Ecuación_7.dig as structural Verilog
module \Ecuación_7  (
  input  C,
  input  B,
  input  A,
  output Y
);

  wire and_1_out, nor_1_out, or_1_out;

  or or_1 (or_1_out, B, C);
  and and_1 (and_1_out, A, B);
  nor nor_1 (nor_1_out, and_1_out, C);
  nand nand_1 (Y, or_1_out, nor_1_out);

  // Notes on the sheet:
  //   Y = not((B or C) and not((A and B) or C)))
endmodule

/* Test case Ecuacion 7:
C B A Y 

 0 0 0 1
 0 0 1 1
 0 1 0 0
 0 1 1 1
 1 0 0 1
 1 0 1 1
 1 1 0 1
 1 1 1 1
*/
