// Digital circuit Ecuación_8.dig as structural Verilog
module \Ecuación_8  (
  input  D,
  input  C,
  input  B,
  input  A,
  output Y
);

  wire and_1_out, and_2_out, nand_1_out, not_2_out, not_4_out, or_1_out, or_2_out, or_3_out;

  // Not not_1 has open pins: in=D, out=open
  not not_2 (not_2_out, C);
  // Not not_3 has open pins: in=B, out=open
  not not_4 (not_4_out, A);
  or or_1 (or_1_out, C, D);
  nand nand_1 (nand_1_out, B, not_2_out);
  and and_1 (and_1_out, A, nand_1_out);
  or or_2 (or_2_out, or_1_out, and_1_out);
  and and_2 (and_2_out, not_4_out, B);
  or or_3 (or_3_out, and_2_out, C);
  and and_3 (Y, or_2_out, or_3_out);

  // Notes on the sheet:
  //   Y = ((C + D) +( A . not(B . not C) and (B . not A)+C)
endmodule

/* Test case Ecuacion 8:
D C B A Y 

 0 0 0 0 0
 0 0 0 1 0
 0 0 1 0 0
 0 0 1 1 0
 0 1 0 0 1
 0 1 0 1 1
 0 1 1 0 1
 0 1 1 1 1
 1 0 0 0 0
 1 0 0 1 0
 1 0 1 0 1
 1 0 1 1 0
 1 1 0 0 1
 1 1 0 1 1
 1 1 1 0 1
 1 1 1 1 1
*/
