// Digital circuit Ecuación_9.dig as structural Verilog
module \Ecuación_9  (
  input  D,
  input  C,
  input  B,
  input  A,
  output Y
);

  wire and_1_out, and_2_out, nand_1_out, nand_2_out, not_1_out, not_2_out, xor_1_out;

  not not_1 (not_1_out, D);
  not not_2 (not_2_out, C);
  // Not not_3 has open pins: in=B, out=open
  // Not not_4 has open pins: in=A, out=open
  and and_1 (and_1_out, A, not_2_out);
  and and_2 (and_2_out, A, B);
  nand nand_1 (nand_1_out, C, not_1_out);
  xor xor_1 (xor_1_out, and_1_out, and_2_out);
  nand nand_2 (nand_2_out, A, nand_1_out);
  and and_3 (Y, xor_1_out, nand_2_out);

  // Notes on the sheet:
  //   Y = ((A . not C) xor (A . B)) . (not(A . not(C . not D)))
endmodule

/* Test case Ecuacion 9:
D C B A Y 

 0 0 0 0 0
 0 0 0 1 0
 0 0 1 0 0
 0 0 1 1 0
 0 1 0 0 0
 0 1 0 1 0
 0 1 1 0 0
 0 1 1 1 1
 1 0 0 0 0
 1 0 0 1 0
 1 0 1 0 0
 1 0 1 1 0
 1 1 0 0 0
 1 1 0 1 0
 1 1 1 0 0
 1 1 1 1 0
*/
