// Digital circuit 00.dig as structural Verilog
module _00 (
  input  C,
  input  B,
  input  A,
  input  C0,
  input  A0,
  output Z,
  output Y,
  output Z0,
  output Y0
);

  wire and_1_out, and_2_out, and_3_out, and_4_out, and_5_out, and_6_out, not_1_out, not_2_out, not_3_out,
       not_4_out, not_5_out, or_1_out, or_2_out;

  not not_1 (not_1_out, C);
  not not_2 (not_2_out, B);
  not not_3 (not_3_out, C0);
  not not_4 (not_4_out, A0);
  not not_5 (not_5_out, A);
  and and_1 (and_1_out, A0, not_3_out);
  and and_2 (and_2_out, not_4_out, C0);
  and and_3 (and_3_out, A0, not_3_out);
  and and_4 (and_4_out, not_4_out, C0);
  and and_5 (and_5_out, not_1_out, A);
  and and_6 (and_6_out, C, not_5_out);
  or or_1 (or_1_out, not_1_out, not_5_out);
  or or_2 (or_2_out, C, A);
  or or_3 (Z0, and_1_out, and_2_out);
  or or_4 (Y0, and_3_out, and_4_out);
  or or_5 (Z, and_5_out, and_6_out);
  and and_7 (Y, or_1_out, or_2_out);

  // Notes on the sheet:
  //   Simplificado
  //   Z = (A !C) + (!A C)
  //   Y = (A !C) + (!A C)
endmodule

/* Test case Testbench:
C B A Z Y 

 0 0 0 0 0
 0 0 1 1 1
 0 1 0 0 0
 0 1 1 1 1
 1 0 0 1 1
 1 0 1 0 0
 1 1 0 1 1
 1 1 1 0 0
*/
