// Digital circuit 00_FPGA.dig as structural Verilog
module _00_FPGA (
  input  C,
  input  B,
  input  A,
  input  C0,
  input  A0,
  output Z,
  output Y,
  output Z0,
  output Y0
);

  main #(.applicationType("GHDL"), .CodeFile("C:\\Users\\black\\OneDrive\\Documentos\\00_FPGA.vhdl")) u_main (
    .C(C), .B(B), .A(A), .C0(C0), .A0(A0), .Z(Z), .Y(Y), .Z0(Z0), .Y0(Y0));

  // Notes on the sheet:
  //   Z = (A !C) + (!A C)
  //   Y = (A !C) + (!A C)
endmodule

/* Test case Testbench:
C B A Z Y 

 0 0 0 0 0
 0 0 1 1 1
 0 1 0 0 0
 0 1 1 1 1
 1 0 0 1 1
 1 0 1 0 0
 1 1 0 1 1
 1 1 1 0 0
*/
