// Digital circuit Aprobada.dig as structural Verilog
module Aprobada (
  input  P1,
  input  P2,
  input  R1
);

  wire and_1_out, xor_1_out;

  xor xor_1 (xor_1_out, P1, P2);
  and and_1 (and_1_out, R1, xor_1_out);
  LED TECNICAS_APROBADA (.in(and_1_out));
endmodule
