// Digital circuit Bin_a_Gray.dig as structural Verilog
module Bin_a_Gray (
  input  D,
  input  C,
  input  B,
  input  A,
  output Z,
  output Y,
  output W,
  output X,
  output Z_2,
  output Y0,
  output W0,
  output X0
);

  wire and_1_out, and_2_out, and_3_out, and_4_out, and_5_out, and_6_out, not_1_out, not_2_out, not_3_out,
       not_4_out;

  not not_1 (not_1_out, D);
  not not_2 (not_2_out, C);
  not not_3 (not_3_out, B);
  not not_4 (not_4_out, A);
  xor xor_1 (Y, D, C);
  xor xor_2 (W, C, B);
  xor xor_3 (X, B, A);
  and and_1 (and_1_out, not_1_out, C);
  and and_2 (and_2_out, D, not_2_out);
  and and_3 (and_3_out, not_2_out, B);
  and and_4 (and_4_out, C, not_3_out);
  and and_5 (and_5_out, not_3_out, A);
  and and_6 (and_6_out, B, not_4_out);
  or or_1 (Y0, and_1_out, and_2_out);
  or or_2 (W0, and_3_out, and_4_out);
  or or_3 (X0, and_5_out, and_6_out);

  assign Z = D;
  assign Z_2 = D;

  // Notes on the sheet:
  //   Bin a Gray
  //   Z = D
  //   Y = (C !D) + (!C D)
  //   W = (B !C) + (!B C)
  //   X = (A !B) + (!A B)
  //   Z' = D
  //   Y0 = (C !D) + (!C D)
  //   W0 = (B !C) + (!B C)
  //   X0 = (A !B) + (!A B)
endmodule

/* Test case Testbench:
D C B A Z Y W X Z' Y0 W0 X0 

 0 0 0 0 0 0 0 0 0 0 0 0
 0 0 0 1 0 0 0 1 0 0 0 1
 0 0 1 0 0 0 1 1 0 0 1 1
 0 0 1 1 0 0 1 0 0 0 1 0
 0 1 0 0 0 1 1 0 0 1 1 0
 0 1 0 1 0 1 1 1 0 1 1 1
 0 1 1 0 0 1 0 1 0 1 0 1
 0 1 1 1 0 1 0 0 0 1 0 0
 1 0 0 0 1 1 0 0 1 1 0 0
 1 0 0 1 1 1 0 1 1 1 0 1
 1 0 1 0 1 1 1 1 1 1 1 1
 1 0 1 1 1 1 1 0 1 1 1 0
 1 1 0 0 1 0 1 0 1 0 1 0
 1 1 0 1 1 0 1 1 1 0 1 1
 1 1 1 0 1 0 0 1 1 0 0 1
 1 1 1 1 1 0 0 0 1 0 0 0
*/
