// Digital circuit Bin_a_Gray_FPGA.dig as structural Verilog
module Bin_a_Gray_FPGA (
  input  D,
  input  C,
  input  B,
  input  A,
  output Z,
  output Y,
  output W,
  output X,
  output Z1,
  output Y0,
  output W0,
  output X0
);

  main #(.applicationType("GHDL"), .CodeFile("C:\\Users\\black\\OneDrive\\Documentos\\Bin_a_Gray.vhdl")) u_main (
    .D(D), .C(C), .B(B), .A(A), .Z(Z), .Y(Y), .W(W), .X(X), .Z1(Z1), .Y0(Y0), .W0(W0), .X0(X0));

  // Notes on the sheet:
  //   Bin a Gray
  //   Z = D
  //   Y = (C !D) + (!C D)
  //   W = (B !C) + (!B C)
  //   X = (A !B) + (!A B)
  //   Z' = D
  //   Y0 = (C !D) + (!C D)
  //   W0 = (B !C) + (!B C)
  //   X0 = (A !B) + (!A B)
endmodule

/* Test case Testbench:
D C B A Z Y W X Z1 Y0 W0 X0 

 0 0 0 0 0 0 0 0 0 0 0 0
 0 0 0 1 0 0 0 1 0 0 0 1
 0 0 1 0 0 0 1 1 0 0 1 1
 0 0 1 1 0 0 1 0 0 0 1 0
 0 1 0 0 0 1 1 0 0 1 1 0
 0 1 0 1 0 1 1 1 0 1 1 1
 0 1 1 0 0 1 0 1 0 1 0 1
 0 1 1 1 0 1 0 0 0 1 0 0
 1 0 0 0 1 1 0 0 1 1 0 0
 1 0 0 1 1 1 0 1 1 1 0 1
 1 0 1 0 1 1 1 1 1 1 1 1
 1 0 1 1 1 1 1 0 1 1 1 0
 1 1 0 0 1 0 1 0 1 0 1 0
 1 1 0 1 1 0 1 1 1 0 1 1
 1 1 1 0 1 0 0 1 1 0 0 1
 1 1 1 1 1 0 0 0 1 0 0 0
*/
