// Digital circuit Full_Adder_Tocci_Pag_322.dig as structural Verilog
module Full_Adder_Tocci_Pag_322 (
  input  A,
  input  B,
  input  C_IN,
  output S,
  output C_SAL
);

  wire and_1_out, and_2_out, and_3_out, xor_1_out;

  // Probe on B
  xor xor_1 (xor_1_out, B, C_IN);
  // Probe on C_IN
  and and_1 (and_1_out, B, C_IN);
  and and_2 (and_2_out, B, A);
  and and_3 (and_3_out, C_IN, A);
  // Probe on A
  // Probe on xor_1_out
  // Probe on and_1_out
  // Probe on and_2_out
  // Probe on and_3_out
  xor xor_2 (S, A, xor_1_out);
  or or_1 (C_SAL, and_1_out, and_2_out, and_3_out);
  // Probe on S
  // Probe on C_SAL

  // Notes on the sheet:
  //   Full Adder
  //   FA
endmodule

/* Test case:
A B C_IN S C_SAL 

 0 0 0 0 0
 0 0 1 1 0
 0 1 0 1 0
 0 1 1 0 1
 1 0 0 1 0
 1 0 1 0 1
 1 1 0 0 1
 1 1 1 1 1
*/
