// Digital circuit Funcion_Simplificada_cero.dig as structural Verilog
module Funcion_Simplificada_cero (
  input  A,
  input  B,
  input  C
);

  wire u_Funcion_Simplificada_cero_y;

  Funcion_Simplificada_cero #(.applicationType("GHDL")) u_Funcion_Simplificada_cero (
    .A(A), .B(B), .C(C), .Y(u_Funcion_Simplificada_cero_y));
  LED Y (.in(u_Funcion_Simplificada_cero_y));
endmodule

/* Code of Funcion_Simplificada_cero:
library ieee;
use ieee.std_logic_1164.all;
--use ieee.std_logic_arith.all;
--use ieee.std_logic_unsigned.all;

entity Funcion_Simplificada_cero is
	port ( A, B, C : in std_logic;
		   Y : out std_logic);
end Funcion_Simplificada_cero;

architecture Behavioral of Funcion_Simplificada_cero is

begin
	Y <= not( (not (C and not b)) and (not (B and not A)) and (not (not C and B)));
end Behavioral;
*/
