// Digital circuit GeneradordeParidad_4Ent.dig as structural Verilog
module GeneradordeParidad_4Ent (
  input  clk,
  output [3:0] value
);

  wire clr_out, en_out, u_GeneradordeParidad_4Ent_pp;

  DipSwitch en (.out(en_out));
  DipSwitch clr (.out(clr_out));
  Counter #(.Bits(4), .isProgramCounter("true")) co (.en(en_out), .C(clk), .clr(clr_out), .out(value));  // open: ovf
  // Probe B on value[1]
  // Probe A on value[0]
  // Probe C on value[2]
  GeneradordeParidad_4Ent #(.applicationType("GHDL")) u_GeneradordeParidad_4Ent (
    .A(value[0]), .B(value[1]), .C(value[2]), .D(value[3]), .Pp(u_GeneradordeParidad_4Ent_pp));
  // Probe D on value[3]
  LED Pp (.in(u_GeneradordeParidad_4Ent_pp));

  // Notes on the sheet:
  //   value: value
  //   TIP: Se agregó Contador Binario de 4 bits para mejorar el
  //   diagrama Temporal.
  //   Se activa al encender Enable(en)
  //   Las sondas(?) son para que salga en el diagrama
  //   Se debe destildar "Mostrar en grafico" value, clr.
  //   El orden de las conexiones al diseñar, establecen el orden en el diagrama,
  //   entonces Primero conectamos las entradas(esto incluye las sondas) y por último la salida.
endmodule

/* Code of GeneradordeParidad_4Ent:
library ieee;
use ieee.std_logic_1164.all;
--use ieee.std_logic_arith.all;
--use ieee.std_logic_unsigned.all;

entity GeneradordeParidad_4Ent is
	port ( A, B, C, D : in std_logic;
		   Pp : out std_logic);
end GeneradordeParidad_4Ent;

architecture Behavioral of GeneradordeParidad_4Ent is

begin
	Pp <= D xor C xor B xor A;
end Behavioral;
*/
