// Digital circuit MUX_Senales.dig as structural Verilog
module MUX_Senales (
  input  clk,
  input  A,
  input  B,
  input  C,
  input  Y_2,
  input  A_2,
  input  B_2,
  input  C_2,
  output [2:0] value,
  output Y,
  output Y_3
);

  wire and_1_out, and_2_out, and_3_out, and_4_out, clr_out, en_out, not_1_out, not_2_out, u_MUX_Senales_y,
       xnor_1_out;

  not not_1 (not_1_out, C_2);
  DipSwitch en (.out(en_out));
  DipSwitch clr (.out(clr_out));
  Counter #(.Bits(3), .isProgramCounter("true")) co (.en(en_out), .C(clk), .clr(clr_out), .out(value));  // open: ovf
  not not_2 (not_2_out, C);
  and and_1 (and_1_out, A, not_2_out);
  and and_2 (and_2_out, B, C);
  and and_3 (and_3_out, A_2, not_1_out);
  and and_4 (and_4_out, B_2, C_2);
  // Probe A on value[1]
  // Probe B on value[0]
  // Probe C on value[2]
  xnor xnor_1 (xnor_1_out, and_1_out, Y_2);
  or or_1 (Y_3, and_3_out, and_4_out);
  MUX_Senales #(.applicationType("GHDL")) u_MUX_Senales (.B(value[0]), .A(value[1]), .C(value[2]), .Y(u_MUX_Senales_y));
  or or_2 (Y, xnor_1_out, and_2_out);
  LED u_Y (.in(u_MUX_Senales_y));

  // Notes on the sheet:
  //   value: value
  //   TIP: Se agregó Contador Binario de 3 bits para mejorar el
  //   diagrama Temporal.
  //   Se activa al encender Enable(en)
  //   Las sondas(?) son para que salga en el diagrama
  //   Se debe destildar "Mostrar en grafico" value, clr.
  //   El orden de las conexiones al diseñar, establecen el orden en el diagrama,
  //   entonces Primero conectamos las entradas(esto incluye las sondas) y por último la salida.
  //   Donde esta Y2 e Y1? Agregamos el circuito
  //   El que figura el la teoría Diapositiva 101 Guia 6 VHDL 2021
  //   Creado con Y = (C*!A)+(B*A)
endmodule

/* Code of MUX_Senales:
library ieee;
use ieee.std_logic_1164.all;
--use ieee.std_logic_arith.all;
--use ieee.std_logic_unsigned.all;

entity MUX_Senales is
	port ( B, A, C : in std_logic;
		   Y : out std_logic);
end MUX_Senales;

architecture Behavioral of MUX_Senales is

Signal Y1, Y2 :  std_logic; --Describo todas las señales
begin
	Y <= Y1 or Y2;
	Y1 <= not C and A;
	Y2 <= C and B;
	-- Las 3 asignaciones simples se ejecutan al mismo tiempo
end Behavioral;
*/
