// Digital circuit PARCIAL2_VIEJO_1b.dig as structural Verilog
module PARCIAL2_VIEJO_1b (
  input  J,
  input  K,
  input  D,
  input  C,
  input  CLK,
  output out_6
);

  wire and_1_out, and_2_out, d_ff_1_nq, multiplexer_1_out, not_1_out, or_1_out;

  not not_1 (not_1_out, K);
  and and_1 (and_1_out, d_ff_1_nq, J);
  and and_2 (and_2_out, not_1_out, out_6);
  or or_1 (or_1_out, and_1_out, and_2_out);
  Multiplexer multiplexer_1 (.sel(C), .in_0(D), .in_1(or_1_out), .out(multiplexer_1_out));
  D_FF d_ff_1 (.D(multiplexer_1_out), .C(CLK), .Q(out_6), .nQ(d_ff_1_nq));
endmodule
