// Digital circuit Pepe.dig as structural Verilog
module Pepe (
  input  clk,
  output [3:0] value
);

  wire clr_out, en_out, u_Pepe_q, u_Pepe_s;

  DipSwitch en (.out(en_out));
  DipSwitch clr (.out(clr_out));
  Counter #(.Bits(4), .isProgramCounter("true")) co (.en(en_out), .C(clk), .clr(clr_out), .out(value));  // open: ovf
  // Probe C on value[1]
  // Probe D on value[0]
  // Probe B on value[2]
  Pepe #(.applicationType("GHDL")) u_Pepe (
    .D(value[0]), .C(value[1]), .B(value[2]), .A(value[3]), .Q(u_Pepe_q), .S(u_Pepe_s));
  // Probe A on value[3]
  LED Q (.in(u_Pepe_q));
  LED S (.in(u_Pepe_s));

  // Notes on the sheet:
  //   value: value
  //   TIP: Se agregó Contador Binario de 4 bits para mejorar el
  //   diagrama Temporal.
  //   Se activa al encender Enable(en)
  //   Las sondas(?) son para que salga en el diagrama
  //   Se debe destildar "Mostrar en grafico" value, clr.
  //   El orden de las conexiones al diseñar, establecen el orden en el diagrama,
  //   entonces Primero conectamos las entradas(esto incluye las sondas) y por último la salida.
endmodule

/* Code of Pepe:
library ieee;
use ieee.std_logic_1164.all;
--use ieee.std_logic_arith.all;
--use ieee.std_logic_unsigned.all;

entity Pepe is
	port ( D, C, B, A : in std_logic;
		   Q, S : out std_logic);
end Pepe;

architecture Behavioral of Pepe is

begin
	Q <= D or C;
	S <= B and A;
end Behavioral;
*/
