// Digital circuit c4_ej7.dig as structural Verilog
module c4_ej7 (
  input  C,
  input  B,
  input  A,
  output Y
);

  wire and_1_out, nor_1_out, or_1_out, u_c4_ej7_y;

  and and_1 (and_1_out, A, B);
  or or_1 (or_1_out, B, C);
  c4_ej7 #(.applicationType("GHDL"), .CodeFile("C:\\Users\\black\\Documents\\c4_ej7.vhdl")) u_c4_ej7 (
    .A(A), .B(B), .C(C), .Y(u_c4_ej7_y));
  nor nor_1 (nor_1_out, and_1_out, C);
  LED led_1 (.in(u_c4_ej7_y));
  nand nand_1 (Y, nor_1_out, or_1_out);

  // Notes on the sheet:
  //   Z=not ( (B or C) and not ( (A and B) or C ) )
  //   Este VHDL y su Testbench
  //   fueron creados por Digital,
  //   realizando el circuito desde la
  //   expresión(Analisis->Expresión),
  //   luego (Archivo -> Exportar VHDL)
  //   Tras ello, guarda los 2 archivos.
  //   Para verlo se agrega VHDL -> External File 
  //   en el árbol de componentes,
  //   se selecciona el .vhdl como program
  //   se selecciona GHDL y se pulsa check.
  //   se realizan las conexiones y se simula.
  //   NOTA: Si se quiere usar Analisis
  //   para ver TV, Mapa de Karnaugh, 
  //   circuito con compuertas universales,
  //   TV reducida. se debe copiar y pegar
  //   el FPGA a otro archivo.
endmodule

/* Test case Y:
C B A Y 

 0 0 0 1
 0 0 1 1
 0 1 0 0
 0 1 1 1
 1 0 0 1
 1 0 1 1
 1 1 0 1
 1 1 1 1
*/
