// Digital circuit c4_tp3.dig as structural Verilog
module c4_tp3 (
  input  A,
  input  B,
  input  C,
  input  C_2,
  input  A_2,
  input  C_3,
  input  A_3,
  input  C_4,
  input  B_2,
  input  A_4,
  output Z,
  output Z_2,
  output Z_3,
  output Z_4
);

  wire and_1_out, nand_1_out, not_1_out, not_2_out, not_3_out, or_1_out;

  not not_1 (not_1_out, A);
  and and_1 (and_1_out, not_1_out, B);
  or or_1 (or_1_out, and_1_out, C);
  and and_2 (Z, or_1_out, not_1_out, C);
  not not_2 (not_2_out, A_2);
  and and_3 (Z_2, not_2_out, C_2);
  c4_tp3 #(.applicationType("GHDL")) u_c4_tp3 (.C(C_4), .B(B_2), .A(A_4), .Z(Z_4));
  not not_3 (not_3_out, A_3);
  nand nand_1 (nand_1_out, not_3_out, C_3);
  not not_4 (Z_3, nand_1_out);

  // Notes on the sheet:
  //   TP 3 CLASE 4
  //   Z = (B !A + C) C !A
  //   Expresión Simplificada:
  //   Z = C !A
  //   VHDL
  //   Circuito con compuerta Universal:
  //   Z = C !A
endmodule

/* Code of c4_tp3:
library ieee;
use ieee.std_logic_1164.all;
--use ieee.std_logic_arith.all; --Es propietaria de Xilinx
--use ieee.std_logic_unsigned.all; --Es propietaria de Xilinx
--use ieee.numeric_std.all; --Ambas se reemplazan con se reemplaza con: use ieee.numeric_std.all
-- compilar con ghdl -s --std=08 --ieee=synopsys archivo.vhd si usamos las bibliotecas de Xilnx

entity c4_tp3 is
	port (C, B, A : in std_logic;
	      Z : out std_logic);
end c4_tp3;

architecture RTL of c4_tp3 is

begin
	Z <= ((B and not A) or C) and C and not A;
end RTL;
*/
