// Digital circuit c5_ej1.dig as structural Verilog
module c5_ej1 (
  input  d,
  input  c,
  input  b,
  input  a,
  output z
);

  wire and_1_out, nand_1_out, not_1_out, not_2_out, or_1_out;

  not not_1 (not_1_out, b);
  not not_2 (not_2_out, a);
  and and_1 (and_1_out, not_2_out, c);
  nand nand_1 (nand_1_out, not_1_out, c);
  or or_1 (or_1_out, nand_1_out, d);
  xor xor_1 (z, and_1_out, or_1_out);

  // Notes on the sheet:
  //   Z=(D+!(C& !B)) xor !A & C
endmodule

/* Test case Testbench:
d c b a z 

 0 0 0 0 1
 0 0 0 1 1
 0 0 1 0 1
 0 0 1 1 1
 0 1 0 0 1
 0 1 0 1 0
 0 1 1 0 0
 0 1 1 1 1
 1 0 0 0 1
 1 0 0 1 1
 1 0 1 0 1
 1 0 1 1 1
 1 1 0 0 0
 1 1 0 1 1
 1 1 1 0 0
 1 1 1 1 1
*/
