// Digital circuit c5_ej1_FPGA.dig as structural Verilog
module c5_ej1_FPGA (
  input  D,
  input  C,
  input  B,
  input  A,
  output Z
);

  c5_ej1 #(.applicationType("GHDL"), .CodeFile("C:\\Users\\black\\Documents\\c5_ej1.vhdl")) u_c5_ej1 (
    .d(D), .c(C), .b(B), .a(A), .z(Z));

  // Notes on the sheet:
  //   Z=(D+!(C& !B)) xor !A & C
endmodule
