// Digital circuit c8.dig as structural Verilog
module c8 (
  input  D,
  input  C,
  input  B,
  input  A,
  input  D_2,
  input  C_2,
  input  B_2,
  input  A_2,
  output Y,
  output X,
  output W,
  output Y_2,
  output X_2,
  output W_2
);

  wire and_2_out, and_3_out, and_4_out, nand_2_out, nand_3_out, nand_4_out, nand_5_out, not_1_out, not_2_out,
       not_3_out, not_4_out, not_5_out, not_6_out, not_7_out, not_8_out;

  not not_1 (not_1_out, D);
  not not_2 (not_2_out, D_2);
  not not_3 (not_3_out, C);
  not not_4 (not_4_out, C_2);
  not not_5 (not_5_out, B);
  not not_6 (not_6_out, A);
  not not_7 (not_7_out, B_2);
  or or_1 (Y, A, D);
  and and_1 (X, not_6_out, not_1_out);
  and and_2 (and_2_out, not_6_out, not_3_out, not_1_out);
  and and_3 (and_3_out, not_6_out, not_5_out, not_3_out);
  and and_4 (and_4_out, not_5_out, not_1_out);
  not not_8 (not_8_out, A_2);
  nand nand_1 (Y_2, not_8_out, not_2_out);
  nand nand_2 (nand_2_out, not_8_out, not_2_out);
  nand nand_3 (nand_3_out, not_8_out, not_4_out, not_2_out);
  nand nand_4 (nand_4_out, not_8_out, not_7_out, not_4_out);
  nand nand_5 (nand_5_out, not_7_out, not_2_out);
  or or_2 (W, and_2_out, and_3_out, and_4_out);
  not not_9 (X_2, nand_2_out);
  nand nand_6 (W_2, nand_3_out, nand_4_out, nand_5_out);

  // Notes on the sheet:
  //   Con NAND
endmodule

/* Test case Testbench:
D C B A Y X W 

 0 0 0 0 0 1 1
 0 0 0 1 1 0 1
 0 0 1 0 0 1 1
 0 0 1 1 1 0 0
 0 1 0 0 0 1 1
 0 1 0 1 1 0 1
 0 1 1 0 0 1 0
 0 1 1 1 1 0 0
 1 0 0 0 1 0 1
 1 0 0 1 1 0 0
 1 0 1 0 1 0 0
 1 0 1 1 1 0 0
 1 1 0 0 1 0 0
 1 1 0 1 1 0 0
 1 1 1 0 1 0 0
 1 1 1 1 1 0 0
*/
