// Digital circuit c8_BIN_a_BCD_Natural.dig as structural Verilog
module c8_BIN_a_BCD_Natural (
  input  B3,
  input  B2,
  input  B1,
  input  B0,
  output BIT3,
  output BIT2,
  output BIT1,
  output BIT0,
  output bms_3,
  output bms_2,
  output bms_1,
  output bms_0
);

  wire and_1_out, and_2_out, and_4_out, and_5_out, and_6_out, and_7_out, not_1_out, not_2_out, not_3_out;

  not not_1 (not_1_out, B3);
  not not_2 (not_2_out, B2);
  not not_3 (not_3_out, B1);
  and and_1 (and_1_out, B1, B3);
  and and_2 (and_2_out, B2, B3);
  and and_3 (bms_3, not_3_out, not_2_out, B3);
  and and_4 (and_4_out, B1, B2);
  and and_5 (and_5_out, B2, not_1_out);
  and and_6 (and_6_out, B1, not_1_out);
  and and_7 (and_7_out, not_3_out, B2, B3);
  or or_1 (BIT0, and_1_out, and_2_out);
  or or_2 (bms_2, and_4_out, and_5_out);
  or or_3 (bms_1, and_6_out, and_7_out);

  assign BIT1 = 1'b0;
  assign BIT2 = 1'b0;
  assign BIT3 = 1'b0;
  assign bms_0 = B0;

  // Notes on the sheet:
  //   Bin 4 bits 
  //   Salida: 4 bits MSB y 4 bits msb
endmodule

/* Test case Testbench:
B3 B2 B1 B0 BIT3 BIT2 BIT1 BIT0 bms_3 bms_2 bms_1 bms_0 

 0 0 0 0 0 0 0 0 0 0 0 0
 0 0 0 1 0 0 0 0 0 0 0 1
 0 0 1 0 0 0 0 0 0 0 1 0
 0 0 1 1 0 0 0 0 0 0 1 1
 0 1 0 0 0 0 0 0 0 1 0 0
 0 1 0 1 0 0 0 0 0 1 0 1
 0 1 1 0 0 0 0 0 0 1 1 0
 0 1 1 1 0 0 0 0 0 1 1 1
 1 0 0 0 0 0 0 0 1 0 0 0
 1 0 0 1 0 0 0 0 1 0 0 1
 1 0 1 0 0 0 0 1 0 0 0 0
 1 0 1 1 0 0 0 1 0 0 0 1
 1 1 0 0 0 0 0 1 0 0 1 0
 1 1 0 1 0 0 0 1 0 0 1 1
 1 1 1 0 0 0 0 1 0 1 0 0
 1 1 1 1 0 0 0 1 0 1 0 1
*/
