// Digital circuit c8_BIN_a_BCD_Natural_FPGA.dig as structural Verilog
module c8_BIN_a_BCD_Natural_FPGA (
  input  B3,
  input  B2,
  input  B1,
  input  B0,
  output [3:0] BMS,
  output [3:0] bms_2
);

  main #(.applicationType("GHDL"), .CodeFile("C:\\Users\\black\\Documents\\c8_BIN_a_BCD_Natural.vhdl")) u_main (
    .B3(B3), .B2(B2), .B1(B1), .B0(B0), .BIT3(BMS[3]), .BIT2(BMS[2]), .BIT1(BMS[1]), .BIT0(BMS[0]),
    .bms_3(bms_2[3]), .bms_2(bms_2[2]), .bms_1(bms_2[1]), .bms_0(bms_2[0]));

  // Notes on the sheet:
  //   Bin a BCD Natural
endmodule
