// Digital circuit c8_BIN_a_XS3.dig as structural Verilog
module c8_BIN_a_XS3 (
  input  B3,
  input  B2,
  input  B1,
  input  B0,
  output Y
);

  wire and_1_out, and_2_out, and_3_out, and_4_out, not_1_out, not_2_out, not_3_out, not_4_out;

  not not_1 (not_1_out, B3);
  not not_2 (not_2_out, B2);
  not not_3 (not_3_out, B1);
  not not_4 (not_4_out, B0);
  and and_1 (and_1_out, not_4_out, not_2_out, not_1_out);
  and and_2 (and_2_out, B0, B2, B3);
  and and_3 (and_3_out, not_3_out, not_2_out, not_1_out);
  and and_4 (and_4_out, B1, B2, B3);
  or or_1 (Y, and_1_out, and_2_out, and_3_out, and_4_out);

  // Notes on the sheet:
  //   Binario a XS3
  //   Z = ( !B3 & !B2 & !B1 ) + ( !B3 & !B2 & !B0 ) + ( B3 & B2 & B0 ) + ( B3 & B2 & B1 )
endmodule

/* Test case Testbench:
B3 B2 B1 B0 Y 

 0 0 0 0 1
 0 0 0 1 1
 0 0 1 0 1
 0 0 1 1 0
 0 1 0 0 0
 0 1 0 1 0
 0 1 1 0 0
 0 1 1 1 0
 1 0 0 0 0
 1 0 0 1 0
 1 0 1 0 0
 1 0 1 1 0
 1 1 0 0 0
 1 1 0 1 1
 1 1 1 0 1
 1 1 1 1 1
*/
