// Digital circuit c8_BIN_a_XS3_FPGA.dig as structural Verilog
module c8_BIN_a_XS3_FPGA (
  input  B3,
  input  B2,
  input  B1,
  input  B0,
  output Y
);

  c8_BIN_a_XS3 #(.applicationType("GHDL"), .CodeFile("C:\\Users\\black\\Documents\\c8_BIN_a_XS3.vhdl")) u_c8_BIN_a_XS3 (
    .B3(B3), .B2(B2), .B1(B1), .B0(B0), .Y(Y));

  // Notes on the sheet:
  //   Binario a XS3
  //   Z = ( !B3 & !B2 & !B1 ) + ( !B3 & !B2 & !B0 ) + ( B3 & B2 & B0 ) + ( B3 & B2 & B1 )
endmodule
