// Digital circuit c8_Comparador_2bits_Simplificacion_ceros.dig as structural Verilog
module c8_Comparador_2bits_Simplificacion_ceros (
  input  A,
  input  B,
  input  C,
  input  D,
  output Y
);

  wire not_1_out, not_2_out, or_1_out, or_2_out, or_3_out, or_4_out, or_5_out;

  not not_1 (not_1_out, A);
  not not_2 (not_2_out, B);
  or or_1 (or_1_out, not_1_out, not_2_out);
  or or_2 (or_2_out, not_1_out, D);
  or or_3 (or_3_out, not_2_out, C);
  or or_4 (or_4_out, not_2_out, D);
  or or_5 (or_5_out, C, D);
  and and_1 (Y, or_1_out, or_2_out, or_3_out, or_4_out, or_5_out);

  // Notes on the sheet:
  //   Simplificación por "0"
endmodule

/* Test case Testbench:
D C B A Y 

 0 0 0 0 0
 0 0 0 1 0
 0 0 1 0 0
 0 0 1 1 0
 0 1 0 0 1
 0 1 0 1 0
 0 1 1 0 0
 0 1 1 1 0
 1 0 0 0 1
 1 0 0 1 1
 1 0 1 0 0
 1 0 1 1 0
 1 1 0 0 1
 1 1 0 1 1
 1 1 1 0 1
 1 1 1 1 0
*/
