// Digital circuit c8_Comparador_2bits_Simplificacion_unos.dig as structural Verilog
module c8_Comparador_2bits_Simplificacion_unos (
  input  D,
  input  C,
  input  B,
  input  A,
  output Z
);

  wire and_1_out, and_2_out, and_3_out, not_1_out, not_2_out;

  not not_1 (not_1_out, B);
  not not_2 (not_2_out, A);
  and and_1 (and_1_out, not_2_out, not_1_out, C);
  and and_2 (and_2_out, not_2_out, C, D);
  and and_3 (and_3_out, not_1_out, D);
  or or_1 (Z, and_1_out, and_2_out, and_3_out);

  // Notes on the sheet:
  //   Simplificación por "1"
endmodule

/* Test case Testbench:
D C B A Z 

 0 0 0 0 0
 0 0 0 1 0
 0 0 1 0 0
 0 0 1 1 0
 0 1 0 0 1
 0 1 0 1 0
 0 1 1 0 0
 0 1 1 1 0
 1 0 0 0 1
 1 0 0 1 1
 1 0 1 0 0
 1 0 1 1 0
 1 1 0 0 1
 1 1 0 1 1
 1 1 1 0 1
 1 1 1 1 0
*/
