// Digital circuit c8_FPGA.dig as structural Verilog
module c8_FPGA (
  input  D,
  input  C,
  input  B,
  input  A,
  output Y,
  output W,
  output X
);

  c8 #(.applicationType("GHDL"), .CodeFile("C:\\Users\\black\\Documents\\c8.vhdl")) u_c8 (
    .D(D), .C(C), .B(B), .A(A), .Y(Y), .X(X), .W(W));
endmodule
