// Digital circuit desplazador_a_derecha_n_bits.dig as structural Verilog
module desplazador_a_derecha_n_bits (
  input  [1:0] D,
  input  A0,
  input  A1,
  input  A2,
  input  A3,
  output B3,
  output B2,
  output B1,
  output B0
);

  // Probe on A3
  // Probe on A2
  // Probe on A1
  // Probe on A0
  Multiplexer #(.Selector_Bits(2)) multiplexer_1 (.sel(D), .in_0(A3), .in_1(1'b0), .in_2(1'b0), .in_3(1'b0), .out(B3));
  Multiplexer #(.Selector_Bits(2)) multiplexer_2 (.sel(D), .in_0(A2), .in_1(A3), .in_2(1'b0), .in_3(1'b0), .out(B2));
  Multiplexer #(.Selector_Bits(2)) multiplexer_3 (.sel(D), .in_0(A1), .in_1(A2), .in_2(A3), .in_3(1'b0), .out(B1));
  Multiplexer #(.Selector_Bits(2)) multiplexer_4 (.sel(D), .in_0(A0), .in_1(A1), .in_2(A2), .in_3(A3), .out(B0));
  // Probe D1 D0 on D
  // Probe Bit 3 on B3
  // Probe Bit 2 on B2
  // Probe Bit 1 on B1
  // Probe Bit 0 on B0

  // Notes on the sheet:
  //   Seleccionar cantidad de bits a desplazar a derecha
  //   Entrada de datos
  //   Mux 3
  //   I1
  //   I2
  //   I3
  //   Mux 2
  //   Mux 1
  //   Mux 0
endmodule
