// Logisim project desplazador_a_izquierda_n_bits.circ as structural Verilog: 1 circuit, main circuit main
module main (
  input  [1:0] D21,
  input  A3,
  input  A2,
  input  A1,
  input  A0,
  output out_6,
  output out_7,
  output out_8,
  output out_9
);

  // Probe on D21
  // Probe on A1
  // Probe on A2
  // Probe on A3
  // Probe on A0
  Multiplexer #(.select(2), .enable("false")) multiplexer_1 (
    .in0(A3), .in1(A2), .in2(A1), .in3(A0), .out(out_6), .sel(D21));
  Multiplexer #(.select(2), .enable("false")) multiplexer_2 (
    .in0(A2), .in1(A1), .in2(A0), .in3(1'b0), .out(out_7), .sel(D21));
  Multiplexer #(.select(2), .enable("false")) multiplexer_3 (
    .in0(A1), .in1(A0), .in2(1'b0), .in3(1'b0), .out(out_8), .sel(D21));
  Multiplexer #(.select(2), .enable("false")) multiplexer_4 (
    .in0(A0), .in1(1'b0), .in2(1'b0), .in3(1'b0), .out(out_9), .sel(D21));
  // Probe on out_6
  // Probe on out_7
  // Probe on out_9
  // Probe on out_8

  // Notes on the sheet:
  //   <-----
endmodule
