// Digital circuit ejTeoria.dig as structural Verilog
module ejTeoria (
  input  C,
  input  B,
  input  A,
  output Z
);

  wire not_1_out, not_2_out, not_3_out, or_1_out, or_2_out;

  not not_1 (not_1_out, C);
  not not_2 (not_2_out, B);
  not not_3 (not_3_out, A);
  or or_1 (or_1_out, C, B);
  or or_2 (or_2_out, not_1_out, not_2_out, not_3_out);
  and and_1 (Z, or_1_out, or_2_out);

  // Notes on the sheet:
  //   Z = (!A B) + (B !C) + (!B C)
  //   Z = (!A C) + (B !C) + (!B C)
endmodule

/* Test case Testbench:
C B A Z 

 0 0 0 0
 0 0 1 0
 0 1 0 1
 0 1 1 1
 1 0 0 1
 1 0 1 1
 1 1 0 1
 1 1 1 0
*/
