// Digital circuit ejTeoria_FPGA.dig as structural Verilog
module ejTeoria_FPGA (
  input  C,
  input  B,
  input  A,
  output Z
);

  main #(.applicationType("GHDL"), .CodeFile("C:\\Users\\black\\OneDrive\\Documentos\\ejTeoria.vhdl")) u_main (
    .C(C), .B(B), .A(A), .Z(Z));

  // Notes on the sheet:
  //   Z = (!A B) + (B !C) + (!B C)
  //   Z = (!A C) + (B !C) + (!B C)
endmodule

/* Test case Testbench:
C B A Z 

 0 0 0 0
 0 0 1 0
 0 1 0 1
 0 1 1 1
 1 0 0 1
 1 0 1 1
 1 1 0 1
 1 1 1 0
*/
