// Digital circuit mux2c.dig as structural Verilog
module mux2c (
  input  clk,
  input  C,
  input  B,
  input  A,
  output [2:0] value
);

  wire clr_out, en_out, u_mux2c_2_y, u_mux2c_y;

  DipSwitch en (.out(en_out));
  Counter #(.Bits(3), .isProgramCounter("true")) co (.en(en_out), .C(clk), .clr(clr_out), .out(value));  // open: ovf
  DipSwitch clr (.out(clr_out));
  // Probe B on value[1]
  // Probe C on value[0]
  // Probe A on value[2]
  mux2c #(.applicationType("GHDL")) u_mux2c (.C(value[0]), .B(value[1]), .A(value[2]), .Y(u_mux2c_y));
  LED Y (.in(u_mux2c_y));
  mux2c #(.applicationType("GHDL")) u_mux2c_2 (.C(C), .B(B), .A(A), .Y(u_mux2c_2_y));
  LED Y_2 (.in(u_mux2c_2_y));

  // Notes on the sheet:
  //   value: value
  //   TIP: Se agregó Contador Binario de 3 bits para mejorar el
  //   diagrama Temporal.
  //   Se activa al encender Enable(en)
  //   Las sondas(?) son para que salga en el diagrama
  //   Se debe destildar "Mostrar en grafico" value, clr.
  //   El orden de las conexiones al diseñar, establecen el orden en el diagrama,
  //   entonces Primero conectamos las entradas(esto incluye las sondas) y por último la salida.
  //   Agregadas las entradas con bototones,
  //   solo para comparar
endmodule

/* Code of mux2c:
library ieee;
use ieee.std_logic_1164.all;
--use ieee.std_logic_arith.all;
--use ieee.std_logic_unsigned.all;

entity mux2c is
	port ( C, B, A : in std_logic;
		   Y : out std_logic);
end mux2c;

architecture Behavioral of mux2c is

begin
	Y <= (not C and A) or (C and B);
end Behavioral;
*/
